# Fritzing sketch RedLed (saved by Fritzing 0.9.3b)
circuit board: 8.46667cm x 5.64444cm

parts:
  C_H_I_P_1 = Next Thing Co. C.H.I.P
  R1 = Rotary Potentiometer (Large) [maximum_resistance=100kΩ package=THT]
  R2 = Resistor [tolerance=±5% resistance=100k package=THT]
  R3 = Resistor [tolerance=±5% resistance=330 package=THT]
  LED1 = LED - 3mm [color="Red (633nm)" package="3 mm [THT]"]

nets:
  N1: C_H_I_P_1.VCC-3V3, R2.Pin_1
  N2: C_H_I_P_1.PWM0, LED1.anode
  N3: C_H_I_P_1.GND, R1.leg1, R3.Pin_1
  N4: C_H_I_P_1.LRADC, R1.wiper
  N5: R1.leg2, R2.Pin_0
  N6: R3.Pin_0, LED1.cathode

notes:
  LRADC
  GND
  PWM0
  VCC-3V3
